// Logisim project ALU_GroupXX.circ as structural Verilog: 12 circuits, main circuit main
module main (
  output halt,
  output [8:0] counter,
  output [3:0] op,
  output [11:0] a,
  output [11:0] b,
  output [11:0] oracle,
  output [11:0] result,
  output err_oracle,
  output error,
  output ok,
  output start_delimiter
);

  wire and_1_out, and_2_out, clock_1_out, comparator_1_eq, comparator_2_eq;

  Clock clock_1 (.out(clock_1_out));
  Counter #(.width(9), .max('h1ff), .trigger("falling")) counter_1 (
    .Q(counter), .carry(halt), .clk(clock_1_out));  // open: load, D, count, clr
  RAM #(.addrWidth(12), .dataWidth(4), .bus("separate")) ram_1 (
    .addr({counter, 3'b000}), .data(op), .ld(1'b1));  // open: din, str, sel, clk, clr
  RAM #(.addrWidth(12), .dataWidth(12), .bus("separate")) ram_2 (
    .addr({counter, 3'b001}), .data(a), .ld(1'b1));  // open: din, str, sel, clk, clr
  RAM #(.addrWidth(12), .dataWidth(12), .bus("separate")) ram_3 (
    .addr({counter, 3'b010}), .data(b), .ld(1'b1));  // open: din, str, sel, clk, clr
  RAM #(.addrWidth(12), .dataWidth(12), .bus("separate")) ram_4 (
    .addr({counter, 3'b011}), .data(oracle), .ld(1'b1));  // open: din, str, sel, clk, clr
  RAM #(.addrWidth(12), .dataWidth(1), .bus("separate")) ram_5 (
    .addr({counter, 3'b100}), .data(err_oracle), .ld(1'b1));  // open: din, str, sel, clk, clr
  RAM #(.addrWidth(12), .dataWidth(1), .bus("separate")) ram_6 (
    .addr({counter, 3'b101}), .data(start_delimiter), .ld(1'b1));  // open: din, str, sel, clk, clr
  _12_bit_ALU u_12_bit_alu_1 (.ALU_code(op), .a(a), .b(b), .overflow(error), .result(result));
  Comparator #(.width(1), .mode("unsigned")) comparator_1 (
    .a(error), .b(err_oracle), .eq(comparator_1_eq));  // open: gt, lt
  Comparator #(.width(12)) comparator_2 (.a(result), .b(oracle), .eq(comparator_2_eq));  // open: gt, lt
  and and_1 (and_1_out, comparator_1_eq, error);
  and and_2 (and_2_out, comparator_2_eq, comparator_1_eq, ~error);  // AND_Gate
  or or_1 (ok, and_1_out, and_2_out);

  // Notes on the sheet:
  //   You must complete the circuit '12-bit ALU' instead.
  //   DO NOT EDIT THIS CIRCUIT!
endmodule

module _12_bit_ALU (
  input  [3:0] ALU_code,
  input  [11:0] a,
  input  [11:0] b,
  output [11:0] result,
  output overflow
);

  wire n12_bit_adder_1_overflow, numeric_inverse_1_overflow, shift_left_a_1_overflow, subtraction_1_overflow;
  wire [11:0] and_1_out, equals_1_equals, greater_than_1_greater_than, less_than_1_lesser_than,
       n12_bit_adder_1_sum, not_1_out, not_equal_1_equals, numeric_inverse_1_inverse, or_1_out,
       shift_left_a_1_sla, shift_left_l_1_sl, shift_reight_l_1_sr, shift_right_a_1_sra, subtraction_1_out_3;

  Shift_right_a shift_right_a_1 (.a(a), .SRA(shift_right_a_1_sra));
  Shift_reight_l shift_reight_l_1 (.a(a), .SR(shift_reight_l_1_sr));
  Shift_left_a shift_left_a_1 (.a(a), .SLA(shift_left_a_1_sla), .Overflow(shift_left_a_1_overflow));
  Numeric_inverse numeric_inverse_1 (.a(a), .Overflow(numeric_inverse_1_overflow), .Inverse(numeric_inverse_1_inverse));
  Shift_left_l shift_left_l_1 (.a(a), .SL(shift_left_l_1_sl));
  Greater_than greater_than_1 (.a(a), .b(b), .Greater_than(greater_than_1_greater_than));
  Equals equals_1 (.a(a), .b(b), .Equals(equals_1_equals));
  Not_equal not_equal_1 (.a(a), .b(b), .Equals(not_equal_1_equals));
  assign not_1_out = ~a;  // NOT_Gate not_1, 12 bits wide
  assign or_1_out = a | b;  // OR_Gate or_1, 12 bits wide
  assign and_1_out = b & a;  // AND_Gate and_1, 12 bits wide
  _12_Bit_Adder u_12_bit_adder_1 (.a(b), .b(a), .Overflow(n12_bit_adder_1_overflow), .Sum(n12_bit_adder_1_sum));
  Subtraction subtraction_1 (.a(a), .b(b), .Overflow(subtraction_1_overflow), .out_3(subtraction_1_out_3));
  Less_than less_than_1 (.a(a), .b(b), .Lesser_than(less_than_1_lesser_than));
  Multiplexer #(.select(4), .width(12), .enable("false")) multiplexer_1 (
    .in0({12{1'b0}}), .in1(or_1_out), .in2(and_1_out), .in3(n12_bit_adder_1_sum), .in4(subtraction_1_out_3),
    .in5(less_than_1_lesser_than), .in6(greater_than_1_greater_than), .in7(equals_1_equals),
    .in8(not_equal_1_equals), .in9(not_1_out), .in10(numeric_inverse_1_inverse), .in11(shift_left_l_1_sl),
    .in12(shift_reight_l_1_sr), .in13(shift_left_a_1_sla), .in14(shift_right_a_1_sra), .in15(a),
    .out(result), .sel(ALU_code));
  Multiplexer #(.select(4), .enable("false")) multiplexer_2 (
    .in0(1'b0), .in1(1'b0), .in2(1'b0), .in3(n12_bit_adder_1_overflow), .in4(subtraction_1_overflow),
    .in5(1'b0), .in6(1'b0), .in7(1'b0), .in8(1'b0), .in9(1'b0), .in10(numeric_inverse_1_overflow),
    .in11(1'b0), .in12(1'b0), .in13(shift_left_a_1_overflow), .in14(1'b0), .in15(1'b0), .out(overflow),
    .sel(ALU_code));

  // Notes on the sheet:
  //   This circuit is used as a block in the main circuit, and its layout must remain unchanged. The circuit called "main" should be the main circuit of this file.
  //   Do not change the circuit appearance.
  //   DO NOT CHANGE THE INPUTS AND OUTPUTS OF THIS CIRCUIT!
  //   Do not add/remove inputs or outputs. Do not even change their location or orientation.
endmodule

// sub
module Subtraction (
  input  [11:0] a,
  input  [11:0] b,
  output [11:0] out_3,
  output Overflow
);

  wire and_1_out, n12_bit_adder_1_overflow, n12_bit_adder_2_overflow, or_1_out;
  wire [11:0] n12_bit_adder_1_sum, not_1_out;

  assign not_1_out = ~b;  // NOT_Gate not_1, 12 bits wide
  _12_Bit_Adder u_12_bit_adder_1 (
    .a(not_1_out), .b(12'h1), .Overflow(n12_bit_adder_1_overflow), .Sum(n12_bit_adder_1_sum));
  and and_1 (and_1_out, a[11], ~not_1_out[11]);  // AND_Gate
  or or_1 (or_1_out, n12_bit_adder_1_overflow, n12_bit_adder_2_overflow);
  _12_Bit_Adder u_12_bit_adder_2 (.a(a), .b(n12_bit_adder_1_sum), .Overflow(n12_bit_adder_2_overflow), .Sum(out_3));
  Multiplexer #(.enable("false")) multiplexer_1 (.in0(or_1_out), .in1(1'b0), .out(Overflow), .sel(and_1_out));
endmodule

// lt
module Less_than (
  input  [11:0] a,
  input  [11:0] b,
  output [11:0] Lesser_than
);

  wire and_1_out, nand_1_out, nand_2_out, not_1_out;
  wire [11:0] equals_1_equals, multiplexer_1_out, multiplexer_2_out, multiplexer_3_out, multiplexer_4_out,
       multiplexer_5_out, subtraction_1_out_3, subtraction_2_out_3;

  not not_1 (not_1_out, equals_1_equals[0]);
  Equals equals_1 (.a(b), .b(a), .Equals(equals_1_equals));
  Subtraction subtraction_1 (.a(a), .b(b), .out_3(subtraction_1_out_3));  // open: Overflow
  Subtraction subtraction_2 (.a(a), .b(b), .out_3(subtraction_2_out_3));  // open: Overflow
  Multiplexer #(.width(12), .enable("false")) multiplexer_1 (
    .in0({12{1'b0}}), .in1(12'h1), .out(multiplexer_1_out), .sel(subtraction_1_out_3[11]));
  Multiplexer #(.width(12), .enable("false")) multiplexer_2 (
    .in0({12{1'b0}}), .in1(12'h1), .out(multiplexer_2_out), .sel(subtraction_2_out_3[11]));
  nand nand_1 (nand_1_out, a[11], ~b[11]);  // NAND_Gate
  nand nand_2 (nand_2_out, ~a[11], b[11]);  // NAND_Gate
  and and_1 (and_1_out, a[11], b[11]);
  Multiplexer #(.width(12), .enable("false")) multiplexer_3 (
    .in0(multiplexer_1_out), .in1(multiplexer_2_out), .out(multiplexer_3_out), .sel(and_1_out));
  Multiplexer #(.width(12), .enable("false")) multiplexer_4 (
    .in0({12{1'b0}}), .in1(multiplexer_5_out), .out(multiplexer_4_out), .sel(nand_2_out));
  Multiplexer #(.width(12), .enable("false")) multiplexer_5 (
    .in0({12{1'b0}}), .in1(multiplexer_3_out), .out(multiplexer_5_out), .sel(not_1_out));
  Multiplexer #(.width(12), .enable("false")) multiplexer_6 (
    .in0(12'h1), .in1(multiplexer_4_out), .out(Lesser_than), .sel(nand_1_out));
  // Pins of 1 and 12 bits meet at equals_1_equals
endmodule

// gt
module Greater_than (
  input  [11:0] a,
  input  [11:0] b,
  output [11:0] Greater_than
);

  wire and_1_out, nand_1_out, nand_2_out, not_1_out;
  wire [11:0] equals_1_equals, multiplexer_1_out, multiplexer_2_out, multiplexer_3_out, multiplexer_4_out,
       multiplexer_5_out, subtraction_1_out_3, subtraction_2_out_3;

  Equals equals_1 (.a(b), .b(a), .Equals(equals_1_equals));
  not not_1 (not_1_out, equals_1_equals[0]);
  Subtraction subtraction_1 (.a(a), .b(b), .out_3(subtraction_1_out_3));  // open: Overflow
  Subtraction subtraction_2 (.a(a), .b(b), .out_3(subtraction_2_out_3));  // open: Overflow
  Multiplexer #(.width(12), .enable("false")) multiplexer_1 (
    .in0(12'h1), .in1({12{1'b0}}), .out(multiplexer_1_out), .sel(subtraction_1_out_3[11]));
  Multiplexer #(.width(12), .enable("false")) multiplexer_2 (
    .in0(12'h1), .in1({12{1'b0}}), .out(multiplexer_2_out), .sel(subtraction_2_out_3[11]));
  nand nand_1 (nand_1_out, a[11], ~b[11]);  // NAND_Gate
  nand nand_2 (nand_2_out, ~a[11], b[11]);  // NAND_Gate
  and and_1 (and_1_out, a[11], b[11]);
  Multiplexer #(.width(12), .enable("false")) multiplexer_3 (
    .in0(multiplexer_1_out), .in1(multiplexer_2_out), .out(multiplexer_3_out), .sel(and_1_out));
  Multiplexer #(.width(12), .enable("false")) multiplexer_4 (
    .in0(12'h1), .in1(multiplexer_5_out), .out(multiplexer_4_out), .sel(nand_2_out));
  Multiplexer #(.width(12), .enable("false")) multiplexer_5 (
    .in0({12{1'b0}}), .in1(multiplexer_3_out), .out(multiplexer_5_out), .sel(not_1_out));
  Multiplexer #(.width(12), .enable("false")) multiplexer_6 (
    .in0({12{1'b0}}), .in1(multiplexer_4_out), .out(Greater_than), .sel(nand_1_out));
  // Pins of 1 and 12 bits meet at equals_1_equals
endmodule

// eq
module Equals (
  input  [11:0] a,
  input  [11:0] b,
  output [11:0] Equals
);

  wire nor_1_out;
  wire [11:0] subtraction_1_out_3;

  Subtraction subtraction_1 (.a(a), .b(b), .out_3(subtraction_1_out_3));  // open: Overflow
  nor nor_1 (nor_1_out, subtraction_1_out_3[0], subtraction_1_out_3[1], subtraction_1_out_3[2], subtraction_1_out_3[3], subtraction_1_out_3[4], subtraction_1_out_3[5], subtraction_1_out_3[6], subtraction_1_out_3[7], subtraction_1_out_3[8], subtraction_1_out_3[9], subtraction_1_out_3[10], subtraction_1_out_3[11]);
  Multiplexer #(.width(12), .enable("false")) multiplexer_1 (
    .in0({12{1'b0}}), .in1(12'h1), .out(Equals), .sel(nor_1_out));
endmodule

// neq
module Not_equal (
  input  [11:0] a,
  input  [11:0] b,
  output [11:0] Equals
);

  wire nor_1_out;
  wire [11:0] subtraction_1_out_3;

  Subtraction subtraction_1 (.a(a), .b(b), .out_3(subtraction_1_out_3));  // open: Overflow
  nor nor_1 (nor_1_out, subtraction_1_out_3[0], subtraction_1_out_3[1], subtraction_1_out_3[2], subtraction_1_out_3[3], subtraction_1_out_3[4], subtraction_1_out_3[5], subtraction_1_out_3[6], subtraction_1_out_3[7], subtraction_1_out_3[8], subtraction_1_out_3[9], subtraction_1_out_3[10], subtraction_1_out_3[11]);
  Multiplexer #(.width(12), .enable("false")) multiplexer_1 (
    .in0(12'h1), .in1({12{1'b0}}), .out(Equals), .sel(nor_1_out));
endmodule

// inv
module Numeric_inverse (
  input  [11:0] a,
  output Overflow,
  output [11:0] Inverse
);

  wire [11:0] not_1_out;

  assign not_1_out = ~a;  // NOT_Gate not_1, 12 bits wide
  _12_Bit_Adder u_12_bit_adder_1 (.a(not_1_out), .b(12'h1), .Overflow(Overflow), .Sum(Inverse));
endmodule

// sll
module Shift_left_l (
  input  [11:0] a,
  output [11:0] SL
);


  assign SL = {a[10:0], 1'b0};
endmodule

// srl
module Shift_reight_l (
  input  [11:0] a,
  output [11:0] SR
);


  assign SR = {1'b0, a[11:1]};
endmodule

// sla
module Shift_left_a (
  input  [11:0] a,
  output Overflow,
  output [11:0] SLA
);

  _12_Bit_Adder u_12_bit_adder_1 (.a(a), .b(a), .Overflow(Overflow), .Sum(SLA));
endmodule

// sra
module Shift_right_a (
  input  [11:0] a,
  output [11:0] SRA
);

  wire [11:0] or_1_out, shift_reight_l_1_sr;

  Shift_reight_l shift_reight_l_1 (.a(a), .SR(shift_reight_l_1_sr));
  assign or_1_out = shift_reight_l_1_sr | 12'h800;  // OR_Gate or_1, 12 bits wide
  Multiplexer #(.width(12), .enable("false")) multiplexer_1 (
    .in0(shift_reight_l_1_sr), .in1(or_1_out), .out(SRA), .sel(a[11]));
endmodule
