// Logisim project D_Group18.circ as structural Verilog: 4 circuits, main circuit main
module main (
  output [11:0] pc,
  output [11:0] r0,
  output [11:0] r1,
  output [11:0] r2,
  output [11:0] r3,
  output [11:0] r4,
  output [11:0] r5,
  output [11:0] r6,
  output [11:0] r7,
  output halt
);

  wire brancha, branchr, branchsrc, clock, clock_1_out, controler_1_alurslt, controler_1_alusrc,
       controler_1_memread_memtoreg, controler_1_memwrite, controler_1_pcsave, controler_1_regdst,
       controler_1_regwrite, halt_t, not_1_out, overflow, reset;
  wire [1:0] ExtendSrc;
  wire [2:0] multiplexer_1_out, multiplexer_2_out, multiplexer_3_out;
  wire [3:0] controler_1_aluop;
  wire [11:0] bit_extender_1_out, bit_extender_3_out, bit_extender_4_out, branchv, D, multiplexer_4_out,
       multiplexer_5_out, multiplexer_6_out, multiplexer_7_out, multiplexer_9_out, n12_bit_alu_1_result,
       PC_1, ram_2_data, register_file_1_s;
  wire [11:6] bit_extender_2_out, lui;
  wire [12:0] ram_1_data;

  Halt halt_1 (.instruction(ram_1_data), .clock(clock_1_out), .reset(reset), .halt(halt));
  Clock clock_1 (.out(clock_1_out));
  Button u_reset (.out(reset));
  PC u_pc_1 (.Clock(clock), .Reset(reset), .Branch_Value(branchv), .Br(branchr), .Ba(brancha), .Instruction_Adress(pc));
  and and_1 (clock, ~halt, ~overflow, ~halt_t, clock_1_out);  // AND_Gate
  _12_Bit_Adder u_12_bit_adder_1 (.a(pc), .b(12'h1), .Sum(PC_1));  // open: Overflow
  RAM #(.addrWidth(12), .dataWidth(13), .bus("asynch")) ram_1 (
    .addr(pc), .data(ram_1_data), .sel(1'b1), .ld(1'b1), .clr(reset));
  Multiplexer #(.width(3), .enable("false")) multiplexer_1 (
    .in0(ram_1_data[2:0]), .in1(ram_1_data[8:6]), .out(multiplexer_1_out), .sel(controler_1_memwrite));
  Multiplexer #(.width(3), .enable("false")) multiplexer_2 (
    .in0(ram_1_data[5:3]), .in1(ram_1_data[8:6]), .out(multiplexer_2_out), .sel(controler_1_regdst));
  Multiplexer #(.width(3), .enable("false")) multiplexer_3 (
    .in0(ram_1_data[8:6]), .in1(3'b111), .out(multiplexer_3_out), .sel(controler_1_pcsave));
  Multiplexer #(.width(12), .enable("false")) multiplexer_4 (
    .in0(multiplexer_9_out), .in1(PC_1), .out(multiplexer_4_out), .sel(controler_1_pcsave));
  Controler controler_1 (
    .Instruction(ram_1_data), .ALUOp(controler_1_aluop), .RegWrite(controler_1_regwrite),
    .MemRead_MemtoReg(controler_1_memread_memtoreg), .MemWrite(controler_1_memwrite),
    .ALUSrc(controler_1_alusrc), .ExtendSrc(ExtendSrc), .ALURslt(controler_1_alurslt), .BranchRel(branchr),
    .BranchAbs(brancha), .BranchSrc(branchsrc), .PCSave(controler_1_pcsave), .RegDst(controler_1_regdst),
    .rd(register_file_1_s), .halt(halt_t));
  Register_File register_file_1 (
    .rs(multiplexer_2_out), .rt(multiplexer_1_out), .rd(multiplexer_3_out), .data(multiplexer_4_out),
    .write(controler_1_regwrite), .reset(reset), .S(register_file_1_s), .T(D), .r0(r0), .r1(r1), .r2(r2),
    .r3(r3), .r4(r4), .r5(r5), .r6(r6), .r7(r7), .clock(clock));
  assign bit_extender_1_out = {{9{1'b0}}, ram_1_data[2:0]};  // Bit_Extender bit_extender_1
  assign {bit_extender_2_out, lui} = {{6{1'b0}}, ram_1_data[5:0]};  // Bit_Extender bit_extender_2
  assign bit_extender_3_out = {{6{ram_1_data[5]}}, ram_1_data[5:0]};  // Bit_Extender bit_extender_3
  assign bit_extender_4_out = {{4{1'b0}}, ram_1_data[8:1]};  // Bit_Extender bit_extender_4
  Multiplexer #(.width(12), .enable("false")) multiplexer_5 (
    .in0(D), .in1(multiplexer_6_out), .out(multiplexer_5_out), .sel(controler_1_alusrc));
  Multiplexer #(.select(2), .width(12), .enable("false")) multiplexer_6 (
    .in0(bit_extender_1_out), .in1({bit_extender_2_out, lui}), .in2(bit_extender_3_out),
    .in3(bit_extender_4_out), .out(multiplexer_6_out), .sel(ExtendSrc));
  _12_bit_ALU u_12_bit_alu_1 (
    .ALU_code(controler_1_aluop), .a(register_file_1_s), .b(multiplexer_5_out), .overflow(overflow),
    .result(n12_bit_alu_1_result));
  Multiplexer #(.width(12), .enable("false")) multiplexer_7 (
    .in0(n12_bit_alu_1_result), .in1({lui, {6{1'b0}}}), .out(multiplexer_7_out), .sel(controler_1_alurslt));
  RAM #(.addrWidth(12), .dataWidth(12), .bus("separate")) ram_2 (
    .addr(multiplexer_7_out), .din(D), .data(ram_2_data), .str(controler_1_memwrite), .sel(1'b1),
    .clk(clock), .ld(controler_1_memread_memtoreg), .clr(reset));
  Multiplexer #(.width(12), .enable("false")) multiplexer_8 (
    .in0(multiplexer_9_out), .in1(multiplexer_6_out), .out(branchv), .sel(branchsrc));
  not not_1 (not_1_out, controler_1_memread_memtoreg);
  Multiplexer #(.width(12), .enable("false")) multiplexer_9 (
    .in0(ram_2_data), .in1(multiplexer_7_out), .out(multiplexer_9_out), .sel(not_1_out));

  // Notes on the sheet:
  //   current instruction
  //   clock signal
  //   reset button
  //   DO NOT CHANGE THE INPUTS AND OUTPUTS OF THIS CIRCUIT! Do not add/remove inputs or outputs. Do not even change their location or orientation.
endmodule

module Halt (
  input  [12:0] instruction,
  input  clock,
  input  reset,
  output halt
);

  wire and_1_out, comparator_1_eq, comparator_2_gt, counter_1_carry, or_1_out, or_2_out;
  wire [11:0] counter_1_q;

  Comparator #(.width(13), .mode("unsigned")) comparator_1 (
    .a(instruction), .b({13{1'b0}}), .eq(comparator_1_eq));  // open: gt, lt
  Counter #(.width(12), .max('hfff), .trigger("falling")) counter_1 (
    .Q(counter_1_q), .carry(counter_1_carry), .clk(clock), .clr(reset));  // open: load, D, count
  or or_1 (or_1_out, comparator_1_eq, counter_1_carry);
  Comparator #(.width(12), .mode("unsigned")) comparator_2 (
    .a(counter_1_q), .b({12{1'b0}}), .gt(comparator_2_gt));  // open: eq, lt
  or or_2 (or_2_out, halt, and_1_out);
  and and_1 (and_1_out, or_1_out, comparator_2_gt);
  Register #(.width(1)) register_1 (.D(or_2_out), .Q(halt), .clk(clock), .clr(reset));  // open: en

  // Notes on the sheet:
  //   halt becomes and stays asserted if the instruction is 0000 (not in the first clock cycle) or the end of the counter is reached (2^12)
endmodule

module PC (
  input  Clock,
  input  Reset,
  input  Br,
  input  [11:0] Branch_Value,
  input  Ba,
  output [11:0] Instruction_Adress
);

  wire [11:0] multiplexer_1_out, multiplexer_2_out, n12_bit_adder_1_sum, n12_bit_adder_2_sum;

  _12_Bit_Register u_12_bit_register_1 (
    .D(multiplexer_2_out), .write(1'b1), .reset(Reset), .Q(Instruction_Adress), .C(Clock));
  _12_Bit_Adder u_12_bit_adder_1 (.a(Instruction_Adress), .b(12'h1), .Sum(n12_bit_adder_1_sum));  // open: Overflow
  _12_Bit_Adder u_12_bit_adder_2 (
    .a(n12_bit_adder_1_sum), .b(Branch_Value), .Sum(n12_bit_adder_2_sum));  // open: Overflow
  Multiplexer #(.width(12), .enable("false")) multiplexer_1 (
    .in0(n12_bit_adder_1_sum), .in1(n12_bit_adder_2_sum), .out(multiplexer_1_out), .sel(Br));
  Multiplexer #(.width(12), .enable("false")) multiplexer_2 (
    .in0(multiplexer_1_out), .in1(Branch_Value), .out(multiplexer_2_out), .sel(Ba));
endmodule

// Control
module Controler (
  input  [12:0] Instruction,
  input  [11:0] rd,
  output [3:0] ALUOp,
  output ALUSrc,
  output RegWrite,
  output MemWrite,
  output MemRead_MemtoReg,
  output RegDst,
  output [1:0] ExtendSrc,
  output ALURslt,
  output BranchRel,
  output BranchSrc,
  output BranchAbs,
  output PCSave,
  output halt
);

  wire and_4_out, comparator_1_eq, comparator_2_eq, comparator_3_eq, comparator_4_eq, comparator_5_eq,
       comparator_6_eq, comparator_7_eq, comparator_8_eq, comparator_9_eq, comparator_10_eq,
       comparator_11_eq, comparator_12_eq, comparator_13_eq, comparator_14_eq, comparator_15_eq,
       comparator_16_eq, comparator_18_eq, comparator_19_eq, comparator_20_eq, comparator_21_eq,
       comparator_22_eq, comparator_23_eq, comparator_24_eq, comparator_25_eq, comparator_26_eq,
       comparator_27_eq, comparator_28_eq, comparator_29_eq, comparator_30_eq, comparator_31_eq,
       comparator_32_eq, comparator_33_eq, comparator_34_eq, comparator_35_eq, multiplexer_6_out, not_1_out,
       or_2_out, or_3_out, or_7_out;
  wire [1:0] multiplexer_4_out, multiplexer_7_out;
  wire [3:0] bit_extender_1_out, multiplexer_1_out, multiplexer_2_out, multiplexer_5_out;

  assign bit_extender_1_out = {{1{1'b1}}, Instruction[2:0]};  // Bit_Extender bit_extender_1
  Comparator #(.width(4)) comparator_1 (.a(4'b0000), .b(Instruction[12:9]), .eq(comparator_1_eq));  // open: gt, lt
  Multiplexer #(.width(4), .enable("false")) multiplexer_1 (
    .in0(Instruction[12:9]), .in1(bit_extender_1_out), .out(multiplexer_1_out), .sel(comparator_1_eq));
  Comparator #(.width(13)) comparator_2 (.a({13{1'b0}}), .b(Instruction), .eq(comparator_2_eq));  // open: gt, lt
  Comparator #(.width(4)) comparator_3 (.a(4'b1101), .b(Instruction[12:9]), .eq(comparator_3_eq));  // open: gt, lt
  Comparator #(.width(4)) comparator_4 (.a(4'b1011), .b(Instruction[12:9]), .eq(comparator_4_eq));  // open: gt, lt
  Comparator #(.width(4)) comparator_5 (.a(4'b1010), .b(Instruction[12:9]), .eq(comparator_5_eq));  // open: gt, lt
  Comparator #(.width(4)) comparator_6 (.a(4'b1001), .b(Instruction[12:9]), .eq(comparator_6_eq));  // open: gt, lt
  Comparator #(.width(4)) comparator_7 (.a(Instruction[12:9]), .b(4'b1110), .eq(comparator_7_eq));  // open: gt, lt
  Comparator #(.width(4)) comparator_8 (.a(4'b1001), .b(Instruction[12:9]), .eq(comparator_8_eq));  // open: gt, lt
  Comparator #(.width(4)) comparator_9 (.a(4'b1011), .b(Instruction[12:9]), .eq(comparator_9_eq));  // open: gt, lt
  Comparator #(.width(4)) comparator_10 (.a(4'b1110), .b(Instruction[12:9]), .eq(comparator_10_eq));  // open: gt, lt
  Comparator #(.width(4)) comparator_11 (.a(Instruction[12:9]), .b(4'b1101), .eq(comparator_11_eq));  // open: gt, lt
  Comparator #(.width(4)) comparator_12 (.a(Instruction[12:9]), .b(4'b1011), .eq(comparator_12_eq));  // open: gt, lt
  Comparator #(.width(4)) comparator_13 (.a(Instruction[12:9]), .b(4'b1100), .eq(comparator_13_eq));  // open: gt, lt
  Comparator #(.width(4)) comparator_14 (.a(Instruction[12:9]), .b(4'b1101), .eq(comparator_14_eq));  // open: gt, lt
  Comparator #(.width(4)) comparator_15 (.a(Instruction[12:9]), .b(4'b1110), .eq(comparator_15_eq));  // open: gt, lt
  Comparator #(.width(4)) comparator_16 (.a(Instruction[12:9]), .b(4'b1111), .eq(comparator_16_eq));  // open: gt, lt
  Comparator #(.width(4)) comparator_17 (.a(Instruction[12:9]), .b(4'b1100), .eq(ALURslt));  // open: gt, lt
  Comparator #(.width(12)) comparator_18 (.a(rd), .b({12{1'b0}}), .eq(comparator_18_eq));  // open: gt, lt
  Comparator #(.width(4)) comparator_19 (.a(Instruction[12:9]), .b(4'b1101), .eq(comparator_19_eq));  // open: gt, lt
  Comparator #(.width(4)) comparator_20 (.a(Instruction[12:9]), .b(4'b1111), .eq(comparator_20_eq));  // open: gt, lt
  Comparator #(.width(4)) comparator_21 (.a(Instruction[12:9]), .b(4'b1110), .eq(comparator_21_eq));  // open: gt, lt
  Comparator #(.width(4)) comparator_22 (.a(Instruction[12:9]), .b(4'b1111), .eq(comparator_22_eq));  // open: gt, lt
  Comparator #(.width(4)) comparator_23 (.a(Instruction[12:9]), .b(4'b0000), .eq(comparator_23_eq));  // open: gt, lt
  Comparator #(.width(3)) comparator_24 (.a(Instruction[2:0]), .b(3'b000), .eq(comparator_24_eq));  // open: gt, lt
  Comparator #(.width(3)) comparator_25 (.a(Instruction[5:3]), .b(3'b000), .eq(comparator_25_eq));  // open: gt, lt
  not not_1 (not_1_out, comparator_25_eq);
  Multiplexer #(.width(4), .enable("false")) multiplexer_2 (
    .in0(multiplexer_1_out), .in1(4'b0000), .out(multiplexer_2_out), .sel(comparator_2_eq));
  or or_1 (ALUSrc, comparator_3_eq, comparator_4_eq, comparator_5_eq, comparator_6_eq, comparator_7_eq);
  Comparator #(.width(4)) comparator_26 (.a(4'b1010), .b(Instruction[12:9]), .eq(comparator_26_eq));  // open: gt, lt
  Multiplexer #(.enable("false")) multiplexer_3 (.in0(1'b0), .in1(1'b1), .out(MemRead_MemtoReg), .sel(comparator_8_eq));
  or or_2 (or_2_out, comparator_12_eq, comparator_13_eq);
  or or_3 (or_3_out, comparator_14_eq, comparator_15_eq);
  and and_1 (BranchRel, ~comparator_18_eq, comparator_19_eq);  // AND_Gate
  or or_4 (BranchAbs, comparator_21_eq, comparator_22_eq);
  and and_2 (PCSave, comparator_22_eq, Instruction[0]);
  and and_3 (halt, comparator_23_eq, not_1_out, comparator_24_eq);
  Comparator #(.width(4)) comparator_27 (.a(4'b1110), .b(Instruction[12:9]), .eq(comparator_27_eq));  // open: gt, lt
  Comparator #(.width(4)) comparator_28 (.a(4'b1101), .b(Instruction[12:9]), .eq(comparator_28_eq));  // open: gt, lt
  Comparator #(.width(4)) comparator_29 (.a(4'b1010), .b(Instruction[12:9]), .eq(comparator_29_eq));  // open: gt, lt
  Comparator #(.width(4)) comparator_30 (.a(Instruction[12:9]), .b(4'b1001), .eq(comparator_30_eq));  // open: gt, lt
  or or_5 (RegDst, comparator_9_eq, comparator_10_eq, comparator_11_eq);
  Multiplexer #(.width(2), .enable("false")) multiplexer_4 (
    .in0(2'b00), .in1(2'b01), .out(multiplexer_4_out), .sel(or_2_out));
  or or_6 (BranchSrc, BranchRel, comparator_20_eq);
  or or_7 (or_7_out, comparator_30_eq, comparator_29_eq, comparator_28_eq, comparator_27_eq);
  Multiplexer #(.width(4), .enable("false")) multiplexer_5 (
    .in0(multiplexer_2_out), .in1(4'b0011), .out(multiplexer_5_out), .sel(or_7_out));
  Multiplexer #(.enable("false")) multiplexer_6 (
    .in0(1'b1), .in1(1'b0), .out(multiplexer_6_out), .sel(comparator_26_eq));
  not not_2 (MemWrite, multiplexer_6_out);
  Multiplexer #(.width(2), .enable("false")) multiplexer_7 (
    .in0(multiplexer_4_out), .in1(2'b10), .out(multiplexer_7_out), .sel(or_3_out));
  Multiplexer #(.width(2), .enable("false")) multiplexer_8 (
    .in0(multiplexer_7_out), .in1(2'b11), .out(ExtendSrc), .sel(comparator_16_eq));
  Comparator #(.width(4)) comparator_31 (.a(4'b1011), .b(Instruction[12:9]), .eq(comparator_31_eq));  // open: gt, lt
  Comparator #(.width(4)) comparator_32 (.a(4'b1101), .b(Instruction[12:9]), .eq(comparator_32_eq));  // open: gt, lt
  Comparator #(.width(4)) comparator_33 (.a(4'b1110), .b(Instruction[12:9]), .eq(comparator_33_eq));  // open: gt, lt
  Multiplexer #(.width(4), .enable("false")) multiplexer_9 (
    .in0(multiplexer_5_out), .in1(4'b0001), .out(ALUOp), .sel(comparator_31_eq));
  Comparator #(.width(1)) comparator_34 (.a(Instruction[0]), .b(1'b0), .eq(comparator_34_eq));  // open: gt, lt
  Comparator #(.width(4)) comparator_35 (.a(Instruction[12:9]), .b(4'b1111), .eq(comparator_35_eq));  // open: gt, lt
  and and_4 (and_4_out, comparator_35_eq, comparator_34_eq);
  and and_5 (RegWrite, ~and_4_out, ~comparator_32_eq, ~comparator_33_eq, multiplexer_6_out);  // AND_Gate
endmodule
