// Logisim project Memory.circ as structural Verilog: 5 circuits, main circuit 12-Bit Register
// REG
module _12_Bit_Register (
  input  C,
  input  [11:0] D,
  input  write,
  input  reset,
  output [11:0] Q
);

  wire not_1_out;

  not not_1 (not_1_out, C);
  D_Flip_Flop d_ff_1 (.clk(not_1_out), .D(D[0]), .Q(Q[0]), .en(write), .reset(reset));  // open: Qn, preset
  D_Flip_Flop d_ff_2 (.clk(not_1_out), .D(D[1]), .Q(Q[1]), .en(write), .reset(reset));  // open: Qn, preset
  D_Flip_Flop d_ff_3 (.clk(not_1_out), .D(D[2]), .Q(Q[2]), .en(write), .reset(reset));  // open: Qn, preset
  D_Flip_Flop d_ff_4 (.clk(not_1_out), .D(D[3]), .Q(Q[3]), .en(write), .reset(reset));  // open: Qn, preset
  D_Flip_Flop d_ff_5 (.clk(not_1_out), .D(D[4]), .Q(Q[4]), .en(write), .reset(reset));  // open: Qn, preset
  D_Flip_Flop d_ff_6 (.clk(not_1_out), .D(D[5]), .Q(Q[5]), .en(write), .reset(reset));  // open: Qn, preset
  D_Flip_Flop d_ff_7 (.clk(not_1_out), .D(D[6]), .Q(Q[6]), .en(write), .reset(reset));  // open: Qn, preset
  D_Flip_Flop d_ff_8 (.clk(not_1_out), .D(D[7]), .Q(Q[7]), .en(write), .reset(reset));  // open: Qn, preset
  D_Flip_Flop d_ff_9 (.clk(not_1_out), .D(D[8]), .Q(Q[8]), .en(write), .reset(reset));  // open: Qn, preset
  D_Flip_Flop d_ff_10 (.clk(not_1_out), .D(D[9]), .Q(Q[9]), .en(write), .reset(reset));  // open: Qn, preset
  D_Flip_Flop d_ff_11 (.clk(not_1_out), .D(D[10]), .Q(Q[10]), .en(write), .reset(reset));  // open: Qn, preset
  D_Flip_Flop d_ff_12 (.clk(not_1_out), .D(D[11]), .Q(Q[11]), .en(write), .reset(reset));  // open: Qn, preset
endmodule

module Register_File (
  input  [2:0] rs,
  input  [2:0] rt,
  input  [2:0] rd,
  input  [11:0] data,
  input  write,
  input  reset,
  output [11:0] S,
  output [11:0] T
);

  wire and_1_out, and_2_out, and_3_out, and_4_out, and_5_out, and_6_out, and_7_out, clock_1_out,
       decoder_1_out1, decoder_1_out2, decoder_1_out3, decoder_1_out4, decoder_1_out5, decoder_1_out6,
       decoder_1_out7;
  wire [11:0] n12_bit_register_1_q, n12_bit_register_2_q, n12_bit_register_3_q, n12_bit_register_4_q,
       n12_bit_register_5_q, n12_bit_register_6_q, n12_bit_register_7_q, n12_bit_register_8_q;

  Clock clock_1 (.out(clock_1_out));
  Decoder #(.select(3), .enable("false")) decoder_1 (
    .out1(decoder_1_out1), .out2(decoder_1_out2), .out3(decoder_1_out3), .out4(decoder_1_out4),
    .out5(decoder_1_out5), .out6(decoder_1_out6), .out7(decoder_1_out7), .sel(rd));  // open: out0
  and and_1 (and_1_out, decoder_1_out1, write);
  and and_2 (and_2_out, decoder_1_out2, write);
  and and_3 (and_3_out, decoder_1_out3, write);
  and and_4 (and_4_out, decoder_1_out4, write);
  and and_5 (and_5_out, decoder_1_out5, write);
  and and_6 (and_6_out, decoder_1_out6, write);
  and and_7 (and_7_out, decoder_1_out7, write);
  _12_Bit_Register u_12_bit_register_1 (
    .D(data), .write(1'b0), .reset(reset), .Q(n12_bit_register_1_q), .C(clock_1_out));
  _12_Bit_Register u_12_bit_register_2 (
    .D(data), .write(and_1_out), .reset(reset), .Q(n12_bit_register_2_q), .C(clock_1_out));
  _12_Bit_Register u_12_bit_register_3 (
    .D(data), .write(and_2_out), .reset(reset), .Q(n12_bit_register_3_q), .C(clock_1_out));
  _12_Bit_Register u_12_bit_register_4 (
    .D(data), .write(and_3_out), .reset(reset), .Q(n12_bit_register_4_q), .C(clock_1_out));
  _12_Bit_Register u_12_bit_register_5 (
    .D(data), .write(and_4_out), .reset(reset), .Q(n12_bit_register_5_q), .C(clock_1_out));
  _12_Bit_Register u_12_bit_register_6 (
    .D(data), .write(and_5_out), .reset(reset), .Q(n12_bit_register_6_q), .C(clock_1_out));
  _12_Bit_Register u_12_bit_register_7 (
    .D(data), .write(and_6_out), .reset(reset), .Q(n12_bit_register_7_q), .C(clock_1_out));
  _12_Bit_Register u_12_bit_register_8 (
    .D(data), .write(and_7_out), .reset(reset), .Q(n12_bit_register_8_q), .C(clock_1_out));
  Multiplexer #(.select(3), .width(12), .enable("false")) multiplexer_1 (
    .in0(n12_bit_register_1_q), .in1(n12_bit_register_2_q), .in2(n12_bit_register_3_q),
    .in3(n12_bit_register_4_q), .in4(n12_bit_register_5_q), .in5(n12_bit_register_6_q),
    .in6(n12_bit_register_7_q), .in7(n12_bit_register_8_q), .out(T), .sel(rt));
  Multiplexer #(.select(3), .width(12), .enable("false")) multiplexer_2 (
    .in0(n12_bit_register_1_q), .in1(n12_bit_register_2_q), .in2(n12_bit_register_3_q),
    .in3(n12_bit_register_4_q), .in4(n12_bit_register_5_q), .in5(n12_bit_register_6_q),
    .in6(n12_bit_register_7_q), .in7(n12_bit_register_8_q), .out(S), .sel(rs));
endmodule

module Counter (
  input  clock,
  input  [11:0] D,
  output [11:0] out_3
);

  wire comparator_1_eq, comparator_1_gt, or_1_out;
  wire [11:0] n12_bit_adder_1_sum;

  _12_Bit_Adder u_12_bit_adder_1 (.a(12'h1), .b(out_3), .Sum(n12_bit_adder_1_sum));  // open: Overflow
  or or_1 (or_1_out, comparator_1_gt, comparator_1_eq);
  Comparator #(.width(12)) comparator_1 (.a(out_3), .b(D), .gt(comparator_1_gt), .eq(comparator_1_eq));  // open: lt
  _12_Bit_Register u_12_bit_register_1 (.D(n12_bit_adder_1_sum), .write(1'b1), .reset(or_1_out), .Q(out_3), .C(clock));
endmodule

module Finit_State_machine (
  input  [11:0] in_1,
  output [11:0] out_2
);

  wire and_1_out, and_2_out, and_3_out, clock_1_out, comparator_1_eq, comparator_1_gt, comparator_1_lt,
       comparator_2_eq, comparator_2_gt, comparator_2_lt, comparator_3_eq, comparator_3_gt, comparator_3_lt,
       comparator_4_eq, comparator_4_gt, comparator_4_lt, comparator_5_eq, comparator_5_gt, comparator_5_lt,
       or_1_out, or_2_out, or_3_out, or_4_out, or_5_out, or_6_out;
  wire [11:0] counter_1_out_3;

  Clock clock_1 (.out(clock_1_out));
  _12_Bit_Register u_12_bit_register_1 (.D(counter_1_out_3), .write(1'b1), .reset(1'b0), .Q(out_2), .C(clock_1_out));
  Comparator #(.width(12)) comparator_1 (
    .a(12'h8), .b(out_2), .gt(comparator_1_gt), .eq(comparator_1_eq), .lt(comparator_1_lt));
  Comparator #(.width(12)) comparator_2 (
    .a(12'hc), .b(out_2), .gt(comparator_2_gt), .eq(comparator_2_eq), .lt(comparator_2_lt));
  Comparator #(.width(12)) comparator_3 (
    .a(12'he), .b(out_2), .gt(comparator_3_gt), .eq(comparator_3_eq), .lt(comparator_3_lt));
  Comparator #(.width(12)) comparator_4 (
    .a(12'h16), .b(out_2), .gt(comparator_4_gt), .eq(comparator_4_eq), .lt(comparator_4_lt));
  Comparator #(.width(12)) comparator_5 (
    .a(12'h1a), .b(out_2), .gt(comparator_5_gt), .eq(comparator_5_eq), .lt(comparator_5_lt));
  Counter counter_1 (.clock(clock_1_out), .D(in_1), .out_3(counter_1_out_3));
  and and_1 (and_1_out, comparator_3_lt, comparator_4_gt);
  and and_2 (and_2_out, comparator_4_lt, comparator_5_gt);
  and and_3 (and_3_out, comparator_1_lt, comparator_2_gt);
  or or_1 (or_1_out, comparator_2_eq, comparator_2_lt);
  or or_2 (or_2_out, comparator_3_eq, and_1_out);
  or or_3 (or_3_out, comparator_4_eq, and_2_out);
  or or_4 (or_4_out, comparator_5_eq, comparator_5_lt);
  or or_5 (or_5_out, comparator_1_eq, and_3_out);
  LED led_1 (.in(comparator_1_gt));
  LED led_2 (.in(or_5_out));
  LED led_3 (.in(or_1_out));
  LED led_4 (.in(or_2_out));
  LED led_5 (.in(or_3_out));
  LED led_6 (.in(or_6_out));
  or or_6 (or_6_out, comparator_3_gt, or_4_out);
endmodule

module _12_Bit_Stack (
  input  push,
  input  pop,
  input  [11:0] data,
  input  reset,
  output error,
  output [11:0] error_2,
  output [11:0] TOS
);

  wire clock_1_out, clock_2_out, clock_3_out, not_1_out, or_1_out, or_2_out;
  wire [11:0] multiplexer_1_out, multiplexer_2_out, multiplexer_3_out, multiplexer_4_out,
       n12_bit_adder_1_sum, ram_1_data, subtraction_1_out_3;

  _12_Bit_Adder u_12_bit_adder_1 (.a(12'h1), .b(error_2), .Sum(n12_bit_adder_1_sum));  // open: Overflow
  Subtraction subtraction_1 (.a(error_2), .b(12'h1), .out_3(subtraction_1_out_3));  // open: Overflow
  Multiplexer #(.width(12), .enable("false")) multiplexer_1 (
    .in0(error_2), .in1(subtraction_1_out_3), .out(multiplexer_1_out), .sel(pop));
  or or_1 (or_1_out, pop, push);
  Multiplexer #(.width(12), .enable("false")) multiplexer_2 (
    .in0(multiplexer_1_out), .in1(n12_bit_adder_1_sum), .out(multiplexer_2_out), .sel(push));
  Multiplexer #(.width(12), .enable("false")) multiplexer_3 (
    .in0(multiplexer_2_out), .in1(error_2), .out(multiplexer_3_out), .sel(error));
  and and_1 (error, push, pop);
  or or_2 (or_2_out, push, pop);
  Multiplexer #(.width(12), .enable("false")) multiplexer_4 (
    .in0(data), .in1({12{1'b0}}), .out(multiplexer_4_out), .sel(pop));
  Clock clock_1 (.out(clock_1_out));
  not not_1 (not_1_out, clock_1_out);
  _12_Bit_Register u_12_bit_register_1 (
    .D(multiplexer_3_out), .write(or_2_out), .reset(reset), .Q(error_2), .C(not_1_out));
  RAM #(.addrWidth(12), .dataWidth(12), .bus("separate")) ram_1 (
    .addr(error_2), .din(multiplexer_4_out), .data(ram_1_data), .str(or_1_out), .clk(clock_2_out), .clr(reset));  // open: sel, ld
  Clock clock_2 (.out(clock_2_out));
  Clock clock_3 (.out(clock_3_out));
  _12_Bit_Register u_12_bit_register_2 (.D(ram_1_data), .reset(reset), .Q(TOS), .C(clock_3_out));  // open: write
endmodule
