// Logisim project Project.circ as structural Verilog: 4 circuits, main circuit 1-Bit Adder
module _1_Bit_Adder (
  input  CarryIn,
  input  b,
  input  a,
  output Sum
);

  wire and_1_out, and_2_out, and_3_out, and_4_out;

  and and_1 (and_1_out, ~a, ~b, CarryIn);  // AND_Gate
  and and_2 (and_2_out, ~a, b, ~CarryIn);  // AND_Gate
  and and_3 (and_3_out, a, ~b, ~CarryIn);  // AND_Gate
  and and_4 (and_4_out, a, b, CarryIn);
  or or_1 (Sum, and_1_out, and_2_out, and_3_out, and_4_out);
endmodule

module _4_Bit_Adder (
  input  CarryIn,
  input  [3:0] a,
  input  [3:0] b,
  output [3:0] Sum,
  output P,
  output G
);

  wire and_5_out, and_6_out, and_7_out, and_8_out, and_9_out, and_10_out, and_12_out, and_13_out, and_14_out;
  wire [2:0] c1_out;
  wire [3:0] and_1_out, or_1_out;

  or or_1 (or_1_out[0], b[0], a[0]);
  or or_2 (or_1_out[1], b[1], a[1]);
  or or_3 (or_1_out[2], b[2], a[2]);
  or or_4 (or_1_out[3], b[3], a[3]);
  and and_1 (and_1_out[0], b[0], a[0]);
  and and_2 (and_1_out[1], b[1], a[1]);
  and and_3 (and_1_out[2], b[2], a[2]);
  and and_4 (and_1_out[3], b[3], a[3]);
  _1_Bit_Adder u_1_bit_adder_1 (.b(a[3]), .a(b[3]), .Sum(Sum[3]), .CarryIn(c1_out[2]));
  and and_5 (and_5_out, CarryIn, or_1_out[0]);
  and and_6 (and_6_out, CarryIn, or_1_out[0], or_1_out[1]);
  and and_7 (and_7_out, and_1_out[0], or_1_out[1]);
  and and_8 (and_8_out, CarryIn, or_1_out[0], or_1_out[1], or_1_out[2]);
  and and_9 (and_9_out, and_1_out[0], or_1_out[1], or_1_out[2]);
  and and_10 (and_10_out, and_1_out[1], or_1_out[2]);
  and and_11 (P, or_1_out[0], or_1_out[1], or_1_out[2], or_1_out[3]);
  and and_12 (and_12_out, and_1_out[0], or_1_out[1], or_1_out[2], or_1_out[3]);
  and and_13 (and_13_out, and_1_out[1], or_1_out[2], or_1_out[3]);
  and and_14 (and_14_out, and_1_out[2], or_1_out[3]);
  _1_Bit_Adder u_1_bit_adder_2 (.b(a[2]), .a(b[2]), .Sum(Sum[2]), .CarryIn(c1_out[1]));
  or c1 (c1_out[0], and_5_out, and_1_out[0]);
  or c2 (c1_out[1], and_6_out, and_7_out, and_1_out[1]);
  or c3 (c1_out[2], and_8_out, and_9_out, and_10_out, and_1_out[2]);
  or or_5 (G, and_12_out, and_13_out, and_14_out, and_1_out[3]);
  _1_Bit_Adder u_1_bit_adder_3 (.b(a[1]), .a(b[1]), .Sum(Sum[1]), .CarryIn(c1_out[0]));
  _1_Bit_Adder u_1_bit_adder_4 (.b(a[0]), .a(b[0]), .Sum(Sum[0]), .CarryIn(CarryIn));
endmodule

module Carry_lookahead_unit (
  input  [2:0] G,
  input  [2:0] P,
  output [2:0] CarryOut,
  output Overflow
);

  wire and_1_out, and_2_out, and_3_out, and_4_out, and_5_out, and_6_out;

  and and_1 (and_1_out, P[0], P[0]);
  and and_2 (and_2_out, P[0], P[0], P[1]);
  and and_3 (and_3_out, G[0], P[1]);
  and and_4 (and_4_out, P[0], P[0], P[1], P[2]);
  and and_5 (and_5_out, G[0], P[1], P[2]);
  and and_6 (and_6_out, G[1], P[2]);
  or C1 (CarryOut[1], and_1_out, G[0]);
  or C2 (CarryOut[2], and_2_out, and_3_out, G[1]);
  or C3 (Overflow, and_4_out, and_5_out, and_6_out, G[2]);

  assign CarryOut[0] = P[0];
  // also tied to GND on the sheet: P[0]
endmodule

module _12_Bit_Adder (
  input  [11:0] a,
  input  [11:0] b,
  output Overflow,
  output [11:0] Sum
);

  wire [2:0] carry_lookahead_unit_1_carryout, n4_bit_adder_3_g, n4_bit_adder_3_p;

  _4_Bit_Adder u_4_bit_adder_1 (
    .a(b[11:8]), .b(a[11:8]), .Sum(Sum[11:8]), .CarryIn(carry_lookahead_unit_1_carryout[2]),
    .P(n4_bit_adder_3_p[2]), .G(n4_bit_adder_3_g[2]));
  Carry_lookahead_unit carry_lookahead_unit_1 (
    .G(n4_bit_adder_3_g), .P(n4_bit_adder_3_p), .Overflow(Overflow),
    .CarryOut(carry_lookahead_unit_1_carryout));
  _4_Bit_Adder u_4_bit_adder_2 (
    .a(b[7:4]), .b(a[7:4]), .Sum(Sum[7:4]), .CarryIn(carry_lookahead_unit_1_carryout[1]),
    .P(n4_bit_adder_3_p[1]), .G(n4_bit_adder_3_g[1]));
  _4_Bit_Adder u_4_bit_adder_3 (
    .a(b[3:0]), .b(a[3:0]), .Sum(Sum[3:0]), .CarryIn(carry_lookahead_unit_1_carryout[0]),
    .P(n4_bit_adder_3_p[0]), .G(n4_bit_adder_3_g[0]));
endmodule
