// Logisim project SD_Group18.circ as structural Verilog: 4 circuits, main circuit main
module main (
  output [11:0] pc,
  output [11:0] r0,
  output [11:0] r1,
  output [11:0] r2,
  output [11:0] r3,
  output [11:0] r4,
  output [11:0] r5,
  output [11:0] r6,
  output [11:0] r7,
  output halt
);

  wire clock, clock_1_out, controler_1_alusrc, controler_1_memread_memtoreg, controler_1_memwrite,
       controler_1_regwrite, not_1_out, reset;
  wire [3:0] controler_1_aluop;
  wire [11:0] bit_extender_1_out, multiplexer_1_out, multiplexer_2_out, n12_bit_alu_1_result, ram_2_data,
       register_file_1_s, register_file_1_t;
  wire [12:0] ram_1_data;

  Halt halt_1 (.instruction(ram_1_data), .clock(clock_1_out), .reset(reset), .halt(halt));
  Clock clock_1 (.out(clock_1_out));
  Button u_reset (.out(reset));
  and and_1 (clock, ~halt, clock_1_out);  // AND_Gate
  PC pc_1 (.Clock(clock), .Reset(reset), .Br(1'b0), .Ba(1'b0), .Instruction_Adress(pc));  // open: Branch_Value
  RAM #(.addrWidth(12), .dataWidth(13), .bus("asynch")) ram_1 (
    .addr(pc), .data(ram_1_data), .sel(1'b1), .ld(1'b1));  // open: clr
  Controler controler_1 (
    .Instruction(ram_1_data), .ALUOp(controler_1_aluop), .RegWrite(controler_1_regwrite),
    .MemRead_MemtoReg(controler_1_memread_memtoreg), .MemWrite(controler_1_memwrite),
    .ALUSrc(controler_1_alusrc));
  Register_File register_file_1 (
    .rs(ram_1_data[5:3]), .rt(ram_1_data[2:0]), .rd(ram_1_data[8:6]), .data(multiplexer_2_out),
    .write(controler_1_regwrite), .reset(reset), .S(register_file_1_s), .T(register_file_1_t), .r0(r0),
    .r1(r1), .r2(r2), .r3(r3), .r4(r4), .r5(r5), .r6(r6), .r7(r7), .clock(clock));
  assign bit_extender_1_out = {{9{1'b0}}, ram_1_data[2:0]};  // Bit_Extender bit_extender_1
  _12_bit_ALU u_12_bit_alu_1 (
    .ALU_code(controler_1_aluop), .a(register_file_1_s), .b(multiplexer_1_out), .result(n12_bit_alu_1_result));  // open: overflow
  Multiplexer #(.width(12), .enable("false")) multiplexer_1 (
    .in0(register_file_1_t), .in1(bit_extender_1_out), .out(multiplexer_1_out), .sel(controler_1_alusrc));
  RAM #(.addrWidth(12), .dataWidth(12), .bus("separate")) ram_2 (
    .addr(n12_bit_alu_1_result), .din(register_file_1_s), .data(ram_2_data), .str(controler_1_memwrite),
    .sel(1'b1), .clk(clock), .ld(controler_1_memread_memtoreg), .clr(reset));
  not not_1 (not_1_out, controler_1_memread_memtoreg);
  Multiplexer #(.width(12), .enable("false")) multiplexer_2 (
    .in0(ram_2_data), .in1(n12_bit_alu_1_result), .out(multiplexer_2_out), .sel(not_1_out));

  // Notes on the sheet:
  //   current instruction
  //   clock signal
  //   reset button
  //   DO NOT CHANGE THE INPUTS AND OUTPUTS OF THIS CIRCUIT! Do not add/remove inputs or outputs. Do not even change their location or orientation.
endmodule

module Halt (
  input  [12:0] instruction,
  input  clock,
  input  reset,
  output halt
);

  wire and_1_out, comparator_1_eq, comparator_2_gt, counter_1_carry, or_1_out, or_2_out;
  wire [11:0] counter_1_q;

  Comparator #(.width(13), .mode("unsigned")) comparator_1 (
    .a(instruction), .b({13{1'b0}}), .eq(comparator_1_eq));  // open: gt, lt
  Counter #(.width(12), .max('hfff), .trigger("falling")) counter_1 (
    .Q(counter_1_q), .carry(counter_1_carry), .clk(clock), .clr(reset));  // open: load, D, count
  or or_1 (or_1_out, comparator_1_eq, counter_1_carry);
  Comparator #(.width(12), .mode("unsigned")) comparator_2 (
    .a(counter_1_q), .b({12{1'b0}}), .gt(comparator_2_gt));  // open: eq, lt
  or or_2 (or_2_out, halt, and_1_out);
  and and_1 (and_1_out, or_1_out, comparator_2_gt);
  Register #(.width(1)) register_1 (.D(or_2_out), .Q(halt), .clk(clock), .clr(reset));  // open: en

  // Notes on the sheet:
  //   halt becomes and stays asserted if the instruction is 0000 (not in the first clock cycle) or the end of the counter is reached (2^12)
endmodule

module PC (
  input  Clock,
  input  Reset,
  input  [11:0] Branch_Value,
  input  Br,
  input  Ba,
  output [11:0] Instruction_Adress
);

  wire [11:0] multiplexer_1_out, multiplexer_2_out, n12_bit_adder_1_sum, n12_bit_adder_2_sum;

  _12_Bit_Register u_12_bit_register_1 (
    .D(multiplexer_2_out), .write(1'b1), .reset(Reset), .Q(Instruction_Adress), .C(Clock));
  _12_Bit_Adder u_12_bit_adder_1 (.a(Instruction_Adress), .b(12'h1), .Sum(n12_bit_adder_1_sum));  // open: Overflow
  _12_Bit_Adder u_12_bit_adder_2 (
    .a(n12_bit_adder_1_sum), .b(Branch_Value), .Sum(n12_bit_adder_2_sum));  // open: Overflow
  Multiplexer #(.width(12), .enable("false")) multiplexer_1 (
    .in0(n12_bit_adder_1_sum), .in1(n12_bit_adder_2_sum), .out(multiplexer_1_out), .sel(Br));
  Multiplexer #(.width(12), .enable("false")) multiplexer_2 (
    .in0(multiplexer_1_out), .in1(Branch_Value), .out(multiplexer_2_out), .sel(Ba));
endmodule

module Controler (
  input  [12:0] Instruction,
  output [3:0] ALUOp,
  output ALUSrc,
  output RegWrite,
  output MemWrite,
  output MemRead_MemtoReg
);

  wire comparator_1_eq, comparator_2_eq, comparator_3_eq, comparator_4_eq, comparator_5_eq, comparator_6_eq,
       comparator_7_eq, comparator_8_eq, or_2_out;
  wire [3:0] bit_extender_1_out, multiplexer_1_out, multiplexer_2_out;

  assign bit_extender_1_out = {{1{1'b1}}, Instruction[2:0]};  // Bit_Extender bit_extender_1
  Comparator #(.width(4)) comparator_1 (.a(4'b0000), .b(Instruction[12:9]), .eq(comparator_1_eq));  // open: gt, lt
  Multiplexer #(.width(4), .enable("false")) multiplexer_1 (
    .in0(Instruction[12:9]), .in1(bit_extender_1_out), .out(multiplexer_1_out), .sel(comparator_1_eq));
  Comparator #(.width(13)) comparator_2 (.a({13{1'b0}}), .b(Instruction), .eq(comparator_2_eq));  // open: gt, lt
  Comparator #(.width(4)) comparator_3 (.a(4'b1010), .b(Instruction[12:9]), .eq(comparator_3_eq));  // open: gt, lt
  Comparator #(.width(4)) comparator_4 (.a(4'b1001), .b(Instruction[12:9]), .eq(comparator_4_eq));  // open: gt, lt
  Comparator #(.width(4)) comparator_5 (.a(4'b1010), .b(Instruction[12:9]), .eq(comparator_5_eq));  // open: gt, lt
  Comparator #(.width(4)) comparator_6 (.a(4'b1001), .b(Instruction[12:9]), .eq(comparator_6_eq));  // open: gt, lt
  Multiplexer #(.width(4), .enable("false")) multiplexer_2 (
    .in0(multiplexer_1_out), .in1(4'b0000), .out(multiplexer_2_out), .sel(comparator_2_eq));
  or or_1 (ALUSrc, comparator_3_eq, comparator_4_eq);
  Multiplexer #(.enable("false")) multiplexer_3 (.in0(1'b1), .in1(1'b0), .out(RegWrite), .sel(comparator_5_eq));
  not not_1 (MemWrite, RegWrite);
  Multiplexer #(.enable("false")) multiplexer_4 (.in0(1'b0), .in1(1'b1), .out(MemRead_MemtoReg), .sel(comparator_6_eq));
  Comparator #(.width(4)) comparator_7 (.a(4'b1010), .b(Instruction[12:9]), .eq(comparator_7_eq));  // open: gt, lt
  Comparator #(.width(4)) comparator_8 (.a(Instruction[12:9]), .b(4'b1001), .eq(comparator_8_eq));  // open: gt, lt
  or or_2 (or_2_out, comparator_8_eq, comparator_7_eq);
  Multiplexer #(.width(4), .enable("false")) multiplexer_5 (
    .in0(multiplexer_2_out), .in1(4'b0011), .out(ALUOp), .sel(or_2_out));
endmodule
