// Logisim project oplossing_project1.circ as structural Verilog: 6 circuits, main circuit main
module main (
  input  in_1,
  input  in_2,
  input  in_3,
  input  in_4,
  input  in_5,
  input  in_6,
  input  in_7,
  input  in_8,
  input  in_9,
  input  in_10,
  input  in_11,
  input  in_12,
  input  in_13,
  output out_14,
  output out_15,
  output out_16,
  output out_17,
  output out_18,
  output out_19,
  output out_20
);

  wire and_2_out, nand_1_out_3, nand_3_out_3, nand_4_out_3, not_1_out, not_2_out, not_4_out, not_5_out,
       or_1_out;

  not not_1 (not_1_out, in_5);
  not not_2 (not_2_out, in_7);
  \nand  nand_1 (.in_1(in_11), .in_2(in_12), .out_3(nand_1_out_3));
  \nand  nand_2 (.in_1(in_13), .in_2(in_13), .out_3(out_20));
  or or_1 (or_1_out, in_1, in_3);
  and and_1 (out_16, not_1_out, not_2_out);
  \nand  nand_3 (.in_1(in_9), .in_2(in_9), .out_3(nand_3_out_3));
  \nand  nand_4 (.in_1(in_10), .in_2(in_10), .out_3(nand_4_out_3));
  not not_3 (out_15, or_1_out);
  \nand  nand_5 (.in_1(nand_3_out_3), .in_2(nand_4_out_3), .out_3(out_18));
  \nand  nand_6 (.in_1(nand_1_out_3), .in_2(nand_1_out_3), .out_3(out_19));
  and and_2 (and_2_out, in_2, in_4);
  not not_4 (not_4_out, in_6);
  not not_5 (not_5_out, in_8);
  or or_2 (out_17, not_4_out, not_5_out);
  not not_6 (out_14, and_2_out);

  // Notes on the sheet:
  //   And
  //   Or
  //   not
endmodule

module \nand  (
  input  in_1,
  input  in_2,
  output out_3
);

  wire and_1_out;

  and and_1 (and_1_out, in_1, in_2);
  not not_1 (out_3, and_1_out);

  // Notes on the sheet:
  //   nand
endmodule

module oef_3 (
  input  in_1,
  input  in_2,
  input  in_3,
  output out_4,
  output out_5
);

  wire and_1_out, and_2_out, and_3_out, and_4_out, not_1_out, not_2_out, not_3_out, not_4_out;

  not not_1 (not_1_out, in_2);
  not not_2 (not_2_out, in_2);
  not not_3 (not_3_out, in_2);
  not not_4 (not_4_out, in_3);
  and and_1 (and_1_out, in_1, not_2_out, in_3);
  and and_2 (and_2_out, not_4_out, not_1_out);
  and and_3 (and_3_out, in_2, in_3);
  and and_4 (and_4_out, in_1, not_3_out, in_3);
  or or_1 (out_4, and_1_out, and_2_out);
  or or_2 (out_5, and_3_out, and_4_out);

  // Notes on the sheet:
  //   oef 3
endmodule

module oef_4 (
  input  A,
  input  B,
  input  C
);

  wire and_1_out, and_2_out, and_3_out, and_4_out, and_5_out, and_6_out, and_7_out, and_8_out, and_9_out,
       and_10_out, and_11_out, and_12_out, and_13_out, and_14_out, and_15_out, and_16_out, not_1_out,
       not_2_out, not_3_out, not_4_out, not_5_out, not_6_out, not_7_out, not_8_out, not_9_out, not_10_out,
       not_11_out, not_12_out, not_13_out, not_14_out, not_15_out, not_16_out, not_17_out, not_18_out,
       not_19_out, not_20_out, not_21_out, not_22_out, not_23_out, not_24_out, not_25_out, not_26_out,
       or_1_out, or_2_out, or_3_out, or_4_out, or_5_out, or_6_out;

  not not_1 (not_1_out, A);
  not not_2 (not_2_out, B);
  not not_3 (not_3_out, B);
  not not_4 (not_4_out, C);
  not not_5 (not_5_out, B);
  not not_6 (not_6_out, C);
  not not_7 (not_7_out, A);
  not not_8 (not_8_out, C);
  not not_9 (not_9_out, A);
  not not_10 (not_10_out, B);
  not not_11 (not_11_out, B);
  not not_12 (not_12_out, C);
  not not_13 (not_13_out, A);
  not not_14 (not_14_out, B);
  not not_15 (not_15_out, A);
  not not_16 (not_16_out, B);
  not not_17 (not_17_out, A);
  not not_18 (not_18_out, A);
  not not_19 (not_19_out, B);
  and and_1 (and_1_out, not_1_out, not_2_out, C);
  and and_2 (and_2_out, A, not_3_out, not_4_out);
  and and_3 (and_3_out, A, not_5_out, C);
  and and_4 (and_4_out, A, B, not_6_out);
  and and_5 (and_5_out, not_7_out, B, not_8_out);
  and and_6 (and_6_out, not_9_out, not_10_out, C);
  and and_7 (and_7_out, A, not_11_out, not_12_out);
  and and_8 (and_8_out, A, B, C);
  and and_9 (and_9_out, not_13_out, C);
  and and_10 (and_10_out, A, not_14_out);
  and and_11 (and_11_out, A, B, C);
  and and_12 (and_12_out, not_15_out, not_16_out, C);
  and and_13 (and_13_out, not_17_out, B);
  and and_14 (and_14_out, A, B, C);
  and and_15 (and_15_out, not_18_out, not_19_out);
  and and_16 (and_16_out, A, B, C);
  or or_1 (or_1_out, and_1_out, and_2_out);
  or or_2 (or_2_out, and_3_out, and_4_out);
  or or_3 (or_3_out, and_6_out, and_7_out, and_8_out);
  or or_4 (or_4_out, and_9_out, and_10_out, and_11_out);
  or or_5 (or_5_out, and_12_out, and_13_out, and_14_out);
  or or_6 (or_6_out, and_15_out, and_16_out);
  not not_20 (not_20_out, or_1_out);
  not not_21 (not_21_out, or_2_out);
  not not_22 (not_22_out, and_5_out);
  not not_23 (not_23_out, or_3_out);
  not not_24 (not_24_out, or_4_out);
  not not_25 (not_25_out, or_5_out);
  not not_26 (not_26_out, or_6_out);
  _7_Segment_Display u_7_segment_display_1 (
    .g(not_20_out), .f(not_21_out), .a(not_22_out), .b(not_23_out), .e(not_24_out), .d(not_25_out),
    .c(not_26_out));  // open: dp
endmodule

module tweede_poging_oef_4 (
  input  A,
  input  B,
  input  C
);

  wire and_1_out, and_2_out, and_3_out, and_4_out, and_5_out, and_6_out, and_7_out, and_8_out, and_9_out,
       and_10_out, and_11_out, and_12_out, and_13_out, and_14_out, and_15_out, and_16_out, and_17_out,
       and_18_out, and_19_out, and_20_out, and_21_out, and_22_out, and_23_out, not_1_out, not_2_out,
       not_3_out, not_4_out, not_5_out, not_6_out, not_7_out, not_8_out, not_9_out, not_10_out, not_11_out,
       not_12_out, not_13_out, not_14_out, not_15_out, not_16_out, not_17_out, not_18_out, not_19_out,
       not_20_out, not_21_out, not_22_out, not_23_out, not_24_out, not_25_out, not_26_out, not_27_out,
       not_28_out, or_1_out, or_2_out, or_3_out, or_4_out, or_5_out, or_6_out, or_7_out;

  not not_1 (not_1_out, A);
  not not_2 (not_2_out, B);
  not not_3 (not_3_out, C);
  not not_4 (not_4_out, A);
  not not_5 (not_5_out, B);
  not not_6 (not_6_out, C);
  not not_7 (not_7_out, C);
  not not_8 (not_8_out, A);
  not not_9 (not_9_out, C);
  not not_10 (not_10_out, A);
  not not_11 (not_11_out, B);
  not not_12 (not_12_out, B);
  not not_13 (not_13_out, C);
  not not_14 (not_14_out, A);
  not not_15 (not_15_out, A);
  not not_16 (not_16_out, C);
  not not_17 (not_17_out, A);
  not not_18 (not_18_out, C);
  not not_19 (not_19_out, C);
  not not_20 (not_20_out, A);
  not not_21 (not_21_out, C);
  not not_22 (not_22_out, C);
  not not_23 (not_23_out, B);
  not not_24 (not_24_out, A);
  not not_25 (not_25_out, A);
  not not_26 (not_26_out, B);
  not not_27 (not_27_out, C);
  not not_28 (not_28_out, C);
  and and_1 (and_1_out, not_1_out, B);
  and and_2 (and_2_out, A, not_2_out);
  and and_3 (and_3_out, A, B, not_3_out);
  and and_4 (and_4_out, not_4_out, not_5_out, not_6_out);
  and and_5 (and_5_out, A, B, not_7_out);
  and and_6 (and_6_out, not_8_out, not_9_out);
  and and_7 (and_7_out, not_10_out, B, C);
  and and_8 (and_8_out, A, not_11_out, C);
  and and_9 (and_9_out, A, B);
  and and_10 (and_10_out, not_12_out, not_13_out);
  and and_11 (and_11_out, not_14_out, C);
  and and_12 (and_12_out, not_15_out, B, not_16_out);
  and and_13 (and_13_out, C, B, A);
  and and_14 (and_14_out, not_17_out, not_18_out);
  and and_15 (and_15_out, A, B, not_19_out);
  and and_16 (and_16_out, not_20_out, not_21_out);
  and and_17 (and_17_out, B, not_22_out, A);
  and and_18 (and_18_out, A, not_23_out, C);
  and and_19 (and_19_out, not_24_out, B, C);
  and and_20 (and_20_out, not_25_out, C);
  and and_21 (and_21_out, not_26_out, not_27_out);
  and and_22 (and_22_out, A, C);
  and and_23 (and_23_out, A, B, not_28_out);
  or or_1 (or_1_out, and_1_out, and_2_out, and_3_out);
  or or_2 (or_2_out, and_4_out, and_2_out, and_5_out);
  or or_3 (or_3_out, and_6_out, and_7_out, and_8_out, and_9_out);
  or or_4 (or_4_out, and_10_out, and_11_out, and_12_out, and_13_out);
  or or_5 (or_5_out, and_14_out, and_15_out);
  or or_6 (or_6_out, and_16_out, and_17_out, and_18_out, and_19_out);
  or or_7 (or_7_out, and_20_out, and_21_out, and_22_out, and_23_out);
  _7_Segment_Display u_7_segment_display_1 (
    .g(or_1_out), .f(or_2_out), .a(or_3_out), .b(or_4_out), .e(or_5_out), .d(or_6_out), .c(or_7_out));  // open: dp

  // Notes on the sheet:
  //   e
  //   f
  //   g
  //   a
  //   b
  //   c
  //   d
endmodule

module oef_4_juiste_versie (
  input  [2:0] in_1
);
endmodule
